// Digital circuit Circuito.dig as structural Verilog
module Circuito (
  input  CLOCK,
  input  RESET,
  input  LOAD_ENABLE,
  input  [4:0] REG_SEL,
  output [31:0] PC,
  output [31:0] INSTR,
  output [31:0] ALU_RESULT,
  output [31:0] REG_DEBUG,
  output HAZARD_STALL,
  output HAZARD_FLUSH
);

  wire dmem_we;
  wire [31:0] dmem_addr, dmem_rdata, dmem_wdata, imem_addr, imem_data;

  riscv_cpu #(.applicationType("GHDL"), .ghdlOptions("--std=08 --ieee=synopsys"), .CodeFile("riscv_cpu.vhd")) u_riscv_cpu (
    .clk_i(CLOCK), .reset_i(RESET), .load_enable_i(LOAD_ENABLE), .imem_data_i(imem_data),
    .dmem_rdata_i(dmem_rdata), .reg_sel_i(REG_SEL), .imem_addr_o(imem_addr), .dmem_addr_o(dmem_addr),
    .dmem_wdata_o(dmem_wdata), .dmem_we_o(dmem_we), .pc_debug_o(PC), .instr_debug_o(INSTR),
    .alu_result_debug_o(ALU_RESULT), .reg_debug_o(REG_DEBUG), .hazard_stall_o(HAZARD_STALL),
    .hazard_flush_o(HAZARD_FLUSH));
  ROM #(.AddrBits(8), .Bits(32)) ROM_INSTR (.A(imem_addr[9:2]), .sel(LOAD_ENABLE), .D(imem_data));
  RAMDualPort #(.AddrBits(8), .Bits(32)) RAM_DADOS (
    .A(dmem_addr[9:2]), .Din(dmem_wdata), .str(dmem_we), .C(CLOCK), .ld(LOAD_ENABLE), .D(dmem_rdata));

  // Other names for the same wires on the sheet: alu_debug[31:0] = ALU_RESULT; clk = CLOCK;
  //   ram_addr[7:0] = dmem_addr[9:2]; hz_flush = HAZARD_FLUSH; hz_stall = HAZARD_STALL;
  //   rom_addr[7:0] = imem_addr[9:2]; instr_debug[31:0] = INSTR; load_en = LOAD_ENABLE; pc_debug[31:0] = PC

  // Notes on the sheet:
  //   contents of ROM_INSTR (hex, n*v repeats v):
  //   a00093,1400113,193,208233,1202b3,40228333,20f3b3,20e433,20c4b3,41a023,51a223,61a423,1a503,1505b3,
  //   41a603,81a683,d60733,108663,ff00793,ff00813,100793,1463,200813,300893,63
endmodule
